# Fritzing sketch simon (saved by Fritzing 0.9.2b)
breadboards: 1

parts:
  Composant1 = Arduino Uno (Rev3)
  LED1 = LED - 5mm [color="Red (633nm)" package="5 mm [THT]"]
  S1 = Pushbutton [package="[THT]"]
  R1 = Resistor [tolerance=±5% resistance=220 package=THT]
  R2 = Resistor [tolerance=±5% resistance=220 package=THT]
  D1 = Rectifier Diode [part_number=1N4001 package="300 mil [THT]"]
  S2 = Pushbutton [package="[THT]"]
  LED2 = LED - 5mm [color="Green (570nm)" package="5 mm [THT]"]
  R3 = Resistor [tolerance=±5% resistance=220 package=THT]
  R4 = Resistor [tolerance=±5% resistance=220 package=THT]
  D2 = Rectifier Diode [part_number=1N4001 package="300 mil [THT]"]
  LED3 = LED - 5mm [color="Blue (470nm)" package="5 mm [THT]"]
  D3 = Rectifier Diode [part_number=1N4001 package="300 mil [THT]"]
  R5 = Resistor [tolerance=±5% resistance=220 package=THT]
  S3 = Pushbutton [package="[THT]"]
  R6 = Resistor [tolerance=±5% resistance=220 package=THT]
  R7 = Resistor [tolerance=±5% resistance=220 package=THT]
  R8 = Resistor [tolerance=±5% resistance=220 package=THT]
  D4 = Rectifier Diode [part_number=1N4001 package="300 mil [THT]"]
  S4 = Pushbutton [package="[THT]"]
  LED4 = LED - 5mm [color="Yellow (592nm)" package="5 mm [THT]"]

nets:
  N1: Composant1.D10_PWM/SS, R7.Pin_1, S4.Pin_3, S4.Pin_4
  N2: Composant1.D11_PWM/MOSI, R5.Pin_1, S3.Pin_3, S3.Pin_4
  N3: Composant1.D12/MISO, S1.Pin_3, S1.Pin_4, R1.Pin_1
  N4: Composant1.D13/SCK, S2.Pin_3, S2.Pin_4, R3.Pin_1
  N5: Composant1.D2, D4.anode
  N6: Composant1.D3_PWM, D3.anode
  N7: Composant1.D4, D1.anode
  N8: Composant1.D5_PWM, D2.anode
  N9: Composant1.5V, S1.Pin_1, S1.Pin_2, S2.Pin_1, S2.Pin_2, S3.Pin_1, S3.Pin_2, S4.Pin_1, S4.Pin_2
  N10: Composant1.GND, LED1.anode, LED2.anode, LED3.anode, LED4.anode
  N11: LED1.cathode, R1.Pin_0, R2.Pin_0
  N12: R2.Pin_1, D1.cathode
  N13: LED2.cathode, R3.Pin_0, R4.Pin_0
  N14: R4.Pin_1, D2.cathode
  N15: LED3.cathode, R5.Pin_0, R6.Pin_0
  N16: D3.cathode, R6.Pin_1
  N17: R7.Pin_0, R8.Pin_0, LED4.cathode
  N18: R8.Pin_1, D4.cathode

// code stored in the sketch: simon.ino
/*
  Simon
  plays a sequence and player has to repeat it.

  
  This example code is in the public domain.

 */
const int LED_G = 2;
const int LED_R = 3;
const int LED_B = 4;
const int LED_Y = 5;
const int BUT_G = 10;  //=LED_B+8
const int BUT_R = 11;  //=LED_R+8
const int BUT_B = 12;  //=LED_B+8
const int BUT_Y = 13;  //=LED_Y+8
const int light = 300;
int nbre_seq = 0;
int nbre_boucle = 0;
long seq[10];
boolean attente = false;


// the setup function runs once when you press reset or power the board
void setup() {  
  Serial.begin(9600);
  // initialize digital pin 2 to 5 as an output and 10 to 13 as input
  for (int i=2; i< 6; i++){
    pinMode(i, OUTPUT);
    pinMode(15-i,INPUT);
  }
  nbre_boucle = 0;
  nbre_seq = 0;
  attente = false;
  initLED();
}

void initLED(){
  digitalWrite(LED_G, HIGH);
  delay(light);
  digitalWrite(LED_R, HIGH);
  delay(light);
  digitalWrite(LED_B, HIGH);
  delay(light);
  digitalWrite(LED_Y, HIGH);
  delay(light*4);
  digitalWrite(LED_Y, LOW);
  delay(light);
  digitalWrite(LED_B, LOW);
  delay(light);
  digitalWrite(LED_R, LOW);
  delay(light);
  digitalWrite(LED_G, LOW);
  delay(light*4);
}

// the loop function runs over and over again forever
void loop() {
  
  if (nbre_boucle==10) return;
  
  if (!attente) {
    sequence();
    nbre_boucle++;
    attente = true;
  }
  else{
    getResult();
  }
}


//ajoute un point aléatoire à la séquence précédente et joue l'ensemble de la séquence
void sequence(){
  
  randomSeed(analogRead(0));
  long randNumber = random(2,6);
  
  seq[nbre_seq] = randNumber;

  Serial.print("seq :");

  for(int i=0; i<nbre_seq+1; i++){
    Serial.print(seq[i]);
    Serial.print(" ");
    digitalWrite(seq[i],HIGH);
    delay(light);
    digitalWrite(seq[i],LOW);
    delay(light);
  }
  Serial.println("-");
  nbre_seq++; 
}

void getResult(){
  
  boolean perdu = false;
  
  Serial.print("Res : ");

    int switchstate=0;    
    int but_Y = 0;
    int but_B = 0;
    int but_R = 0;
    int but_G = 0;
  
  for (int i=0; i<nbre_seq; i++){
    int previous = but_Y*LED_Y + but_B*LED_B + but_R*LED_R + but_G*LED_G;
    
    //while(switchstate != 1){
    while(true){
      but_Y = digitalRead(BUT_Y);
      but_B = digitalRead(BUT_B);
      but_R = digitalRead(BUT_R);
      but_G = digitalRead(BUT_G);
      //switchstate = but_Y +but_B + but_R + but_G;
      switchstate = but_Y*LED_Y + but_B*LED_B + but_R*LED_R + but_G*LED_G;
      if (switchstate==0) previous = 0;
      else{
        if (switchstate == previous) continue;
        else break;
      }
    }
    if (but_Y == 1) {
      Serial.print(LED_Y);
      if (seq[i]!=LED_Y) {
        perdu = true;
        but_Y = 0;
      }
    }
     else if (but_B == 1){
       Serial.print(LED_B);
       if (seq[i]!=LED_B) {
        perdu = true;
        but_B = 0;
      }
     }
     else if (but_R == 1){
       Serial.print(LED_R);
       if (seq[i]!=LED_R) {
        perdu = true;
        but_R = 0;
      }
     }
     else if (but_G==1){
       Serial.print(LED_G);
       if (seq[i]!=LED_G) {
          perdu = true;
          but_G = 0;
        }
     }
     
     if(perdu){
       Serial.println(" ! ");
       fin();
       return;
     }
     Serial.print(" ");
  }
  Serial.println("-");
  delay(1000);
  attente = false;
}

void fin(){
  
  for (int i=0; i<5; i++){
    digitalWrite(LED_G, HIGH);
    digitalWrite(LED_R, HIGH);
    digitalWrite(LED_B, HIGH);
    digitalWrite(LED_Y, HIGH);
    delay(2*light);
    digitalWrite(LED_Y, LOW);
    digitalWrite(LED_B, LOW);
    digitalWrite(LED_R, LOW);
    digitalWrite(LED_G, LOW);
    delay(2*light);
  }
  
  setup();
  
}
